# Fritzing sketch treadmill_wiring (saved by Fritzing 0.9.10b)

parts:
  Arduino = Arduino Nano (Rev3.0)
  HX711 = HX711 Weighing Sensor Module
  Load_Cell_50kg_(20VDC) = Load Cell - Red/white/black/green

nets:
  GND: Arduino.GND, HX711.GND, Load_Cell_50kg_(20VDC).GND
  N1: Arduino.D3, HX711.CK/TX
  N2: Arduino.D4, HX711.DO/RX
  5V: Arduino.5V, HX711.VCC
  N3: HX711.E+, Load_Cell_50kg_(20VDC).E+
  N4: HX711.E-, Load_Cell_50kg_(20VDC).E-
  N5: HX711.A+, Load_Cell_50kg_(20VDC).S+
  N6: HX711.A-, Load_Cell_50kg_(20VDC).S-

notes:
  HX711 module
  Load Cell (50kg) 20VDC
  connected to 5V Arduino output (works fine)

custom parts:
  HX711 Weighing Sensor Module: HX711 is a precision 24-bit analog-to-digital converter (ADC) designed for weigh scales and industrial control applications to interface directly with a bridge sensor.
  Load Cell - Red/white/black/green: A rectangle load cell/weighting pressure Sensor with four wires - Red, white, black, green. Normally corresponding with E+, E-, A+, A- respectively.
