# Fritzing sketch treadmill_wiring (saved by Fritzing 0.9.10b)

parts:
  Part1 = Arduino Nano (Rev3.0)
  Load_Cell2 = Load Cell - Red/white/black/green
  Part2 = HX711 Weighing Sensor Module

nets:
  GND: Part1.GND, Part2.GND
  N1: Part1.D3, Part2.CK/TX
  N2: Part1.D4, Part2.DO/RX
  5V: Part1.5V, Part2.VCC
  N3: Load_Cell2.wire1, Part2.E+
  N4: Load_Cell2.wire2, Part2.A-
  N5: Load_Cell2.wire3, Part2.E-
  N6: Load_Cell2.wire4, Part2.A+

notes:
  HX711 module
  Load Cell (50kg) 20VDC
  connected to 5V Arduino output (works fine)

custom parts:
  Load Cell - Red/white/black/green: A rectangle load cell/weighting pressure Sensor with four wires - Red, white, black, green. Normally corresponding with E+, E-, A+, A- respectively.
  HX711 Weighing Sensor Module: HX711 is a precision 24-bit analog-to-digital converter (ADC) designed for weigh scales and industrial control applications to interface directly with a bridge sensor.
